# Fritzing sketch ESP-01 TempNode (saved by Fritzing 0.9.3b)

parts:
  U1 = ESP8266 WiFi Module [part_number=ESP8266-01]
  R1 = Resistor [tolerance=±5% resistance=220 package=THT]
  DS1 = DS18B20 1-Wire Temperature Sensor [part_number=DS18B20]
  DS2 = DS18B20 1-Wire Temperature Sensor [part_number=DS18B20]
  DS3 = DS18B20 1-Wire Temperature Sensor [part_number=DS18B20]
  U2 = V_REG_LD1117VXX [part_number=LD33V package=78xxl]
  C1 = Electrolytic Capacitor [capacitance=1µF package="100 mil [THT, electrolytic]"]
  Power = Power plug [part_number=+5vdc]

nets:
  VDD: U1.VCC, U1.CH_PD, R1.Pin_1, DS1.VDD, DS2.VDD, DS3.VDD, U2.OUT, C1.+
  N1: U1.GPIO_2, R1.Pin_0, DS1.DQ, DS2.DQ, DS3.DQ
  GND: U1.GND, DS1.GND, DS2.GND, DS3.GND, U2.GND, C1.-, Power.GND
  5V: U2.IN, Power.VCC

custom parts:
  ESP8266 WiFi Module: Generic WiFi Module based on the ESP8266 with onboard PCB antenna and UART communications
